// Digital circuit lab04.dig as structural Verilog
module lab04 (
  input  clk,
  input  rst,
  output [31:0] PC,
  output [5:0] opcode,
  output [4:0] src1__addr,
  output [31:0] src1__out,
  output [31:0] src2__addr,
  output [31:0] src2__out,
  output [4:0] dst__addr,
  output [31:0] dst__data
);

  wire and_1_out, u_alu3_zero, u_control_unit_branch, u_control_unit_mem_read, u_control_unit_mem_to_reg,
       u_control_unit_mem_write, u_control_unit_reg_dst, u_control_unit_reg_write;
  wire [1:0] u_control_unit_alu_op;
  wire [3:0] u_alu_control_alu_control;
  wire [15:0] cpumemory_d2;
  wire [31:0] barrelshifter_1_out, bitextender_1_out, cpumemory_d1, multiplexer_1_out, multiplexer_3_out,
       u_alu1_result, u_alu2_result, u_alu3_result;

  BarrelShifter #(.Bits(32)) barrelshifter_1 (.in(bitextender_1_out), .shift(32'h2), .out(barrelshifter_1_out));
  gen_register #(.applicationType("IVERILOG"), .CodeFile("./gen_register.v")) u_gen_register (
    .clk(clk), .rst(rst), .write_en(clk), .data_in(multiplexer_1_out), .data_out(PC));
  alu1 #(.applicationType("IVERILOG"), .CodeFile("./alu.v")) u_alu1 (
    .A(PC), .B(32'h4), .result(u_alu1_result));  // open: alu_control, zero
  RAMDualAccess #(.AddrBits(8), .isProgramMemory("true"), .Bits(32)) cpumemory (
    .str(u_control_unit_mem_write), .C(clk), .ld(u_control_unit_mem_read), .A1(u_alu3_result[7:0]),
    .Din1(src2__addr), .A2(PC[7:0]), .D1(cpumemory_d1),
    .D2({opcode, src1__addr, src2__out[4:0], cpumemory_d2}));
  alu2 #(.applicationType("IVERILOG"), .CodeFile("./alu.v")) u_alu2 (
    .A(u_alu1_result), .B(barrelshifter_1_out), .result(u_alu2_result));  // open: alu_control, zero
  and and_1 (and_1_out, u_control_unit_branch, u_alu3_zero);
  BitExtender #(.inputBits(16), .outputBits(32)) bitextender_1 (.in(cpumemory_d2), .out(bitextender_1_out));
  Multiplexer #(.Bits(32)) multiplexer_1 (
    .sel(and_1_out), .in_0(u_alu1_result), .in_1(u_alu2_result), .out(multiplexer_1_out));
  Multiplexer #(.Bits(5)) multiplexer_2 (
    .sel(u_control_unit_reg_dst), .in_0(opcode[4:0]), .in_1(cpumemory_d2[15:11]), .out(dst__addr));
  control_unit #(.applicationType("IVERILOG"), .CodeFile("./control_unit.v")) u_control_unit (
    .instr_op(opcode), .reg_dst(u_control_unit_reg_dst), .branch(u_control_unit_branch),
    .mem_read(u_control_unit_mem_read), .mem_to_reg(u_control_unit_mem_to_reg),
    .alu_op(u_control_unit_alu_op), .mem_write(u_control_unit_mem_write), .alu_src(bitextender_1_out[0]),
    .reg_write(u_control_unit_reg_write));
  cpu_registers #(.applicationType("IVERILOG"), .CodeFile("./cpu_registers.v")) u_cpu_registers (
    .clk(clk), .rst(rst), .write_en(u_control_unit_reg_write), .src1_addr(src1__addr),
    .src2_addr(src2__out[4:0]), .dst_addr(dst__addr), .data_in(dst__data), .src1_out(src1__out),
    .src2_out(src2__addr));
  alu_control #(.applicationType("IVERILOG"), .CodeFile("./alu_control.v")) u_alu_control (
    .alu_op(u_control_unit_alu_op), .funct(cpumemory_d2[5:0]), .alu_control(u_alu_control_alu_control));
  Multiplexer #(.Bits(32)) multiplexer_3 (
    .sel(bitextender_1_out[0]), .in_0(u_alu3_result), .in_1(cpumemory_d1), .out(multiplexer_3_out));
  alu3 #(.applicationType("IVERILOG"), .CodeFile("./alu.v")) u_alu3 (
    .alu_control(u_alu_control_alu_control), .A(src1__out), .B(multiplexer_3_out), .zero(u_alu3_zero),
    .result(u_alu3_result));
  Multiplexer #(.Bits(32)) multiplexer_4 (
    .sel(u_control_unit_mem_to_reg), .in_0(u_alu3_result), .in_1(cpumemory_d1), .out(dst__data));
  // Pins of 5 and 6 bits meet at opcode
  // Pins of 1 and 32 bits meet at bitextender_1_out
  // Pins of 5 and 32 bits meet at src2__out
  // Pins of 5 and 32 bits meet at src2__addr
  // Pins of 8 and 32 bits meet at u_alu3_result

  // Notes on the sheet:
  //   Inputs
  //   PC
  //   Outputs for testing
endmodule
